// Digital circuit 3bitRegForPc.dig as structural Verilog
module _3bitRegForPc (
  input  [2:0] I_2_0,
  input  CLK,
  output [2:0] O_2_0
);

  _1BitReg _1bitreg_1 (.Din(I_2_0[2]), .Sel(1'b1), .Clk(CLK), .Dout(O_2_0[2]));
  _1BitReg _1bitreg_2 (.Din(I_2_0[1]), .Sel(1'b1), .Clk(CLK), .Dout(O_2_0[1]));
  _1BitReg _1bitreg_3 (.Din(I_2_0[0]), .Sel(1'b1), .Clk(CLK), .Dout(O_2_0[0]));

  // Other names for the same wires on the sheet: B0 = O_2_0[0]; B1 = O_2_0[1]; B2 = O_2_0[2]; A0 = I_2_0[0];
  //   A1 = I_2_0[1]; A2 = I_2_0[2]
endmodule
