// Digital circuit 4BitReg.dig as structural Verilog
module _4BitReg (
  input  [3:0] Din_3_0,
  input  CLK,
  input  Sel,
  output [3:0] Dout_3_0
);

  _1BitReg _1bitreg_1 (.Din(Din_3_0[3]), .Sel(Sel), .Clk(CLK), .Dout(Dout_3_0[3]));
  _1BitReg _1bitreg_2 (.Din(Din_3_0[2]), .Sel(Sel), .Clk(CLK), .Dout(Dout_3_0[2]));
  _1BitReg _1bitreg_3 (.Din(Din_3_0[1]), .Sel(Sel), .Clk(CLK), .Dout(Dout_3_0[1]));
  _1BitReg _1bitreg_4 (.Din(Din_3_0[0]), .Sel(Sel), .Clk(CLK), .Dout(Dout_3_0[0]));

  // Other names for the same wires on the sheet: B0 = Dout_3_0[0]; B1 = Dout_3_0[1]; B2 = Dout_3_0[2];
  //   B3 = Dout_3_0[3]; A0 = Din_3_0[0]; A1 = Din_3_0[1]; A2 = Din_3_0[2]; A3 = Din_3_0[3]
endmodule
