// Digital circuit 4bitAdder.dig as structural Verilog
module _4bitAdder (
  input  [3:0] A_3_0,
  input  [3:0] B_3_0,
  output [3:0] R_3_0,
  output Cout
);

  wire fa_2_cout, fa_3_cout, fa_4_cout;

  FA fa_1 (.X(A_3_0[3]), .Y(B_3_0[3]), .Cin(fa_2_cout), .S(R_3_0[3]), .Cout(Cout));
  FA fa_2 (.X(A_3_0[2]), .Y(B_3_0[2]), .Cin(fa_3_cout), .S(R_3_0[2]), .Cout(fa_2_cout));
  FA fa_3 (.X(A_3_0[1]), .Y(B_3_0[1]), .Cin(fa_4_cout), .S(R_3_0[1]), .Cout(fa_3_cout));
  FA fa_4 (.X(A_3_0[0]), .Y(B_3_0[0]), .Cin(1'b0), .S(R_3_0[0]), .Cout(fa_4_cout));
  // Pins of 1 and 4 bits meet at R_3_0
endmodule
