// Digital circuit 4bitNot.dig as structural Verilog
module _4bitNot (
  input  [3:0] A_3_0,
  output [3:0] R_3_0
);

  not not_1 (R_3_0[0], A_3_0[0]);
  not not_2 (R_3_0[1], A_3_0[1]);
  not not_3 (R_3_0[2], A_3_0[2]);
  not not_4 (R_3_0[3], A_3_0[3]);
endmodule
