// Digital circuit 8x18RAM.dig as structural Verilog
module _8x18RAM (
  input  [17:0] WRD_17_0,
  input  [2:0] WR_2_0,
  input  WE,
  input  [2:0] RA1_2_0,
  input  [2:0] RA2_2_0,
  input  CLK,
  output [17:0] RD1_17_0,
  output [17:0] RD2_17_0
);

  wire D0, D1, D2, D3, D4, D5, D6, D7, RS1_0, RS1_1, RS1_2, RS1_3, RS1_4, RS1_5, RS1_6, RS1_7, RS2_0, RS2_1,
       RS2_2, RS2_3, RS2_4, RS2_5, RS2_6, RS2_7, W0, W1, W2, W3, W4, W5, W6, W7;
  wire [17:0] or_1_out, or_2_out, or_3_out, or_4_out, RD1_0, RD1_1, RD1_2, RD1_3, RD1_4, RD1_5, RD1_6, RD1_7,
       RD2_0, RD2_1, RD2_2, RD2_3, RD2_4, RD2_5, RD2_6, RD2_7;

  and and_1 (D7, W7, WE);
  and and_2 (D6, W6, WE);
  Decoder #(.Selector_Bits(3)) decoder_1 (
    .sel(RA1_2_0), .out_0(RS1_0), .out_1(RS1_1), .out_2(RS1_2), .out_3(RS1_3), .out_4(RS1_4), .out_5(RS1_5),
    .out_6(RS1_6), .out_7(RS1_7));
  Decoder #(.Selector_Bits(3)) decoder_2 (
    .sel(RA2_2_0), .out_0(RS2_0), .out_1(RS2_1), .out_2(RS2_2), .out_3(RS2_3), .out_4(RS2_4), .out_5(RS2_5),
    .out_6(RS2_6), .out_7(RS2_7));
  Decoder #(.Selector_Bits(3)) decoder_3 (
    .sel(WR_2_0), .out_0(W0), .out_1(W1), .out_2(W2), .out_3(W3), .out_4(W4), .out_5(W5), .out_6(W6),
    .out_7(W7));
  and and_3 (D5, W5, WE);
  and and_4 (D4, W4, WE);
  and and_5 (D3, W3, WE);
  and and_6 (D2, W2, WE);
  and and_7 (D1, W1, WE);
  and and_8 (D0, W0, WE);
  _1x18RAM _1x18ram_1 (.RS1(RS1_7), .RS2(RS2_7), .WS(D7), .WD_17_0(WRD_17_0), .CLK(CLK), .RD1(RD1_7), .RD2(RD2_7));
  _1x18RAM _1x18ram_2 (.RS1(RS1_6), .RS2(RS2_6), .WS(D6), .WD_17_0(WRD_17_0), .CLK(CLK), .RD1(RD1_6), .RD2(RD2_6));
  _1x18RAM _1x18ram_3 (.RS1(RS1_5), .RS2(RS2_5), .WS(D5), .WD_17_0(WRD_17_0), .CLK(CLK), .RD1(RD1_5), .RD2(RD2_5));
  _1x18RAM _1x18ram_4 (.RS1(RS1_4), .RS2(RS2_4), .WS(D4), .WD_17_0(WRD_17_0), .CLK(CLK), .RD1(RD1_4), .RD2(RD2_4));
  _1x18RAM _1x18ram_5 (.RS1(RS1_3), .RS2(RS2_3), .WS(D3), .WD_17_0(WRD_17_0), .CLK(CLK), .RD1(RD1_3), .RD2(RD2_3));
  _1x18RAM _1x18ram_6 (.RS1(RS1_2), .RS2(RS2_2), .WS(D2), .WD_17_0(WRD_17_0), .CLK(CLK), .RD1(RD1_2), .RD2(RD2_2));
  _1x18RAM _1x18ram_7 (.RS1(RS1_1), .RS2(RS2_1), .WS(D1), .WD_17_0(WRD_17_0), .CLK(CLK), .RD1(RD1_1), .RD2(RD2_1));
  _1x18RAM _1x18ram_8 (.RS1(RS1_0), .RS2(RS2_0), .WS(D0), .WD_17_0(WRD_17_0), .CLK(CLK), .RD1(RD1_0), .RD2(RD2_0));
  assign or_1_out = RD1_7 | RD1_6 | RD1_5 | RD1_4;  // Or or_1, 18 bits wide
  assign or_2_out = RD1_3 | RD1_2 | RD1_1 | RD1_0;  // Or or_2, 18 bits wide
  assign or_3_out = RD2_7 | RD2_6 | RD2_5 | RD2_4;  // Or or_3, 18 bits wide
  assign or_4_out = RD2_3 | RD2_2 | RD2_1 | RD2_0;  // Or or_4, 18 bits wide
  assign RD1_17_0 = or_1_out | or_2_out;  // Or or_5, 18 bits wide
  assign RD2_17_0 = or_3_out | or_4_out;  // Or or_6, 18 bits wide

  // Other names for the same wires on the sheet: WRD[17:0] = WRD_17_0
endmodule
