// Digital circuit CPU4.dig as structural Verilog
module CPU4 (
  input  [17:0] WRD_17_0,
  input  WE,
  input  [2:0] WR_2_0,
  input  clk,
  input  PC_EN,
  input  [2:0] RA2__2_0,
  input  ZF,
  output [2:0] R2__2_0,
  output [2:0] R1__2_0,
  output [2:0] WR_2_0_2,
  output [17:0] RD2__17_0,
  output [2:0] R2__2_0_2,
  output [2:0] WR__2_0,
  output [3:0] R__3_0,
  output [3:0] A__3_0,
  output [3:0] B__2_0,
  output [2:0] R1__2_0_2,
  output [3:0] IMMI_VAL__3_0,
  output [2:0] JMP_ADDR__2_0
);

  wire CPU_CLK, IMM_SEL, JMP_SEL, REG_EN;
  wire [1:0] Op;
  wire [2:0] _3bitpcadder_1_o_2_0, _3bitregforpc_1_o_2_0, multiplexer_1_out;
  wire [3:0] register_set_6_1_b_3_0;
  wire [6:0] XX;
  wire [17:14] _8x18ram_1_rd1_17_0;

  Multiplexer #(.Bits(3)) multiplexer_1 (
    .sel(JMP_SEL), .in_0(_3bitpcadder_1_o_2_0), .in_1(JMP_ADDR__2_0), .out(multiplexer_1_out));
  _3bitRegForPc _3bitregforpc_1 (.I_2_0(multiplexer_1_out), .CLK(CPU_CLK), .O_2_0(_3bitregforpc_1_o_2_0));
  _3bitPcAdder _3bitpcadder_1 (.I_2_0(_3bitregforpc_1_o_2_0), .O_2_0(_3bitpcadder_1_o_2_0));
  _8x18RAM _8x18ram_1 (
    .RA1_2_0(_3bitregforpc_1_o_2_0), .RA2_2_0(RA2__2_0), .WR_2_0(WR_2_0), .WRD_17_0(WRD_17_0), .WE(WE),
    .CLK(clk), .RD1_17_0({_8x18ram_1_rd1_17_0, JMP_ADDR__2_0, IMMI_VAL__3_0, XX}), .RD2_17_0(RD2__17_0));
  and and_1 (CPU_CLK, PC_EN, clk);
  Register_Set_6 register_set_6_1 (
    .WE(REG_EN), .WRD_3_0(R__3_0), .WR_2_0(JMP_ADDR__2_0), .CLK(CPU_CLK), .A_3_0(A__3_0),
    .B_3_0(register_set_6_1_b_3_0), .RA_2_0(JMP_ADDR__2_0), .RB_2_0(IMMI_VAL__3_0[3:1]));
  _4bitALU _4bitalu_1 (.A_3_0(A__3_0), .B_3_0(B__2_0), .OP_1_0(Op), .R_3_0(R__3_0));
  _4bitCU _4bitcu_1 (
    .Opcode_3_0(_8x18ram_1_rd1_17_0), .ZF(ZF), .Op_1_0(Op), .REG_EN(REG_EN), .Imm_Sel(IMM_SEL),
    .JMP_SEL(JMP_SEL));
  Multiplexer #(.Bits(4)) multiplexer_2 (
    .sel(IMM_SEL), .in_0(register_set_6_1_b_3_0), .in_1(IMMI_VAL__3_0), .out(B__2_0));

  assign R1__2_0 = JMP_ADDR__2_0;
  assign R1__2_0_2 = JMP_ADDR__2_0;
  assign R2__2_0 = IMMI_VAL__3_0[3:1];
  assign R2__2_0_2 = IMMI_VAL__3_0[3:1];
  assign WR_2_0_2 = JMP_ADDR__2_0;
  assign WR__2_0 = JMP_ADDR__2_0;

  // Other names for the same wires on the sheet: XXX[6:0] = XX; XXXX[10:0] = {IMMI_VAL__3_0, XX};
  //   IMMI[3:0] = IMMI_VAL__3_0; XX[7] = IMMI_VAL__3_0[0]; R2[2:0] = IMMI_VAL__3_0[3:1];
  //   JMP_ADDR[2:0] = JMP_ADDR__2_0; R1[2:0] = JMP_ADDR__2_0; AA[3:0] = A__3_0; B[3:0] = B__2_0; R[3:0] = R__3_0;
  //   RD2[17:0] = RD2__17_0

  // Notes on the sheet:
  //   Register Mode (00):    2bit(Type of Op) + 2bit(Op) +3bit(Reg 1) + 3bit(Reg 2) +8 bit(don't care)
  //   Immediate Mode(01):  2bit(Type of Op) + 2bit(Op) +3bit(Reg 1) + 4bit(imm val) + 7 bit(don't care)
  //   Jump Mode(10):           2bit(Type of Op) + 2bit(Op) + 3bit + 11 bit(don't care)
  //   JMP(Op =00), JE(Op = 01)
  //   ADD(Op = 00), ROL(Op =01), NOT(Op = 10)
  //   ADD R1,R2 => 000000100100000000
  //   ADD R1,2   =>  010000100100000000
  //   NOT R1  =>     001000100000000000
  //   JMP to 01 =>  100000000000000000
  //   JE  4th ram slot => 100101100000000000
  //   4th ram slot :
  //   	 ADD R1,2   =>  010000100100000000
endmodule
