// Digital circuit Register Set(6).dig as structural Verilog
module Register_Set_6 (
  input  [3:0] WRD_3_0,
  input  CLK,
  input  [2:0] WR_2_0,
  input  WE,
  input  [2:0] RA_2_0,
  input  [2:0] RB_2_0,
  output [3:0] A_3_0,
  output [3:0] B_3_0
);

  wire A0, A1, A2, A3, A4, A5, D0, D1, D2, D3, D4, D5;
  wire [3:0] R0, R1, R2, R3, R4, R5;

  Decoder #(.Selector_Bits(3)) decoder_1 (
    .sel(WR_2_0), .out_0(A0), .out_1(A1), .out_2(A2), .out_3(A3), .out_4(A4), .out_5(A5));  // open: out_6, out_7
  and and_1 (D5, A5, WE);
  and and_2 (D4, A4, WE);
  and and_3 (D3, A3, WE);
  and and_4 (D2, A2, WE);
  and and_5 (D1, A1, WE);
  and and_6 (D0, A0, WE);
  _4BitReg _4bitreg_1 (.Din_3_0(WRD_3_0), .Sel(D5), .CLK(CLK), .Dout_3_0(R5));
  _4BitReg _4bitreg_2 (.Din_3_0(WRD_3_0), .Sel(D4), .CLK(CLK), .Dout_3_0(R4));
  _4BitReg _4bitreg_3 (.Din_3_0(WRD_3_0), .Sel(D3), .CLK(CLK), .Dout_3_0(R3));
  _4BitReg _4bitreg_4 (.Din_3_0(WRD_3_0), .Sel(D2), .CLK(CLK), .Dout_3_0(R2));
  _4BitReg _4bitreg_5 (.Din_3_0(WRD_3_0), .Sel(D1), .CLK(CLK), .Dout_3_0(R1));
  _4BitReg _4bitreg_6 (.Din_3_0(WRD_3_0), .Sel(D0), .CLK(CLK), .Dout_3_0(R0));
  Multiplexer #(.Selector_Bits(3), .Bits(4)) multiplexer_1 (
    .sel(RA_2_0), .in_0(R0), .in_1(R1), .in_2(R2), .in_3(R3), .in_4(R4), .in_5(R5), .in_6(4'b0000),
    .in_7(4'b0000), .out(A_3_0));
  Multiplexer #(.Selector_Bits(3), .Bits(4)) multiplexer_2 (
    .sel(RB_2_0), .in_0(R0), .in_1(R1), .in_2(R2), .in_3(R3), .in_4(R4), .in_5(R5), .in_6(4'b0000),
    .in_7(4'b0000), .out(B_3_0));
endmodule
